// Logisim project Assignment1.circ as structural Verilog: 11 circuits, main circuit Not
module Not (
  input  in,
  output out
);

  nand nand_1 (out, in, in);

  // Notes on the sheet:
  //   Use only a built-in Nand gate for this (found in Gates>NAND).
  //   Once you are done go to Simulate>Test Vector.
  //   Select the Not.txt file, and run it to try the test cases
endmodule

module And (
  input  a,
  input  b,
  output out
);

  wire nand_1_out;

  nand nand_1 (nand_1_out, a, b);
  Not not_1 (.in(nand_1_out), .out(out));

  // Notes on the sheet:
  //   Simple Gate Implementation using Nand and Not
  //   For all gates in this assignment (except Nand),you are required to use
  //   the custom subcircuits you build, rather than the built-in gates.
endmodule

module Or (
  input  a,
  input  b,
  output out
);

  wire and_1_out, not_1_out, not_2_out;

  Not not_1 (.in(a), .out(not_1_out));
  Not not_2 (.in(b), .out(not_2_out));
  And and_1 (.a(not_1_out), .b(not_2_out), .out(and_1_out));
  Not not_3 (.in(and_1_out), .out(out));

  // Notes on the sheet:
  //   This function can be defined in terms of boolean expressions previously implemented
  //   It helps to start by looking at the expression as Not(Not(A Or B)) and using boolean
  //   algebra to transform this into something we can implement
endmodule

module Xor (
  input  a,
  input  b,
  output out
);

  wire and_1_out, not_1_out, or_1_out;

  And and_1 (.a(a), .b(b), .out(and_1_out));
  Or or_1 (.a(a), .b(b), .out(or_1_out));
  Not not_1 (.in(and_1_out), .out(not_1_out));
  And and_2 (.a(not_1_out), .b(or_1_out), .out(out));

  // Notes on the sheet:
  //   This function can also be defined in terms of boolean expressions already created. 
  //   Try to express what the Xor gate does in english, then translate that to a boolean
  //   expression that you can implement!
endmodule

module Mux (
  input  sel,
  input  a,
  input  b,
  output out
);

  wire and_1_out, and_2_out, not_1_out;

  Not not_1 (.in(sel), .out(not_1_out));
  And and_1 (.a(sel), .b(b), .out(and_1_out));
  And and_2 (.a(not_1_out), .b(a), .out(and_2_out));
  Or or_1 (.a(and_2_out), .b(and_1_out), .out(out));

  // Notes on the sheet:
  //   Function:
  //   If sel == 0, out = a;
  //   	else out = b;
  //   Can be implemented with And, or and Not. Try a truth table!
endmodule

module DMux (
  input  sel,
  input  in,
  output a,
  output b
);

  wire not_1_out;

  Not not_1 (.in(sel), .out(not_1_out));
  And and_1 (.a(not_1_out), .b(in), .out(a));
  And and_2 (.a(sel), .b(in), .out(b));

  // Notes on the sheet:
  //   Function:
  //   If sel == 0, [a, b] = [in, 0]
  //   	else, [a, b] = [0, in]
  //   Same as before, use a truth table and basic logic gates.
endmodule

module Not16 (
  input  [15:0] in,
  output [15:0] out
);

  Not not_1 (.in(in[3]), .out(out[3]));
  Not not_2 (.in(in[3]), .out(out[3]));
  Not not_3 (.in(in[4]), .out(out[4]));
  Not not_4 (.in(in[4]), .out(out[4]));
  Not not_5 (.in(in[13]), .out(out[13]));
  Not not_6 (.in(in[13]), .out(out[13]));
  Not not_7 (.in(in[14]), .out(out[14]));
  Not not_8 (.in(in[0]), .out(out[0]));
  Not not_9 (.in(in[1]), .out(out[1]));
  Not not_10 (.in(in[1]), .out(out[1]));
  Not not_11 (.in(in[2]), .out(out[2]));
  Not not_12 (.in(in[2]), .out(out[2]));
  Not not_13 (.in(in[5]), .out(out[5]));
  Not not_14 (.in(in[5]), .out(out[5]));
  Not not_15 (.in(in[6]), .out(out[6]));
  Not not_16 (.in(in[6]), .out(out[6]));
  Not not_17 (.in(in[7]), .out(out[7]));
  Not not_18 (.in(in[7]), .out(out[7]));
  Not not_19 (.in(in[8]), .out(out[8]));
  Not not_20 (.in(in[9]), .out(out[9]));
  Not not_21 (.in(in[9]), .out(out[9]));
  Not not_22 (.in(in[10]), .out(out[10]));
  Not not_23 (.in(in[10]), .out(out[10]));
  Not not_24 (.in(in[11]), .out(out[11]));
  Not not_25 (.in(in[11]), .out(out[11]));
  Not not_26 (.in(in[12]), .out(out[12]));
  Not not_27 (.in(in[12]), .out(out[12]));
  Not not_28 (.in(in[15]), .out(out[15]));

  // Notes on the sheet:
  //   Function:
  //   For all i from 0 .. 15, out[i] = Not(in[i])
  //   These are rather repetitive, you will use the splitter element (shown below)
  //   a lot. You already have an elementary version of each of these gates, the implementation
  //   of a 16-bit gate is just a matter of constructing an array of n elementary gates, where
  //   each gate operates separately on each bit.
  //   Changing the spacing attribute on the splitter can help a lot for these
endmodule

module And16 (
  input  [15:0] a,
  input  [15:0] b,
  output [15:0] out
);

  And and_1 (.a(a[0]), .b(b[0]), .out(out[0]));
  And and_2 (.a(a[1]), .b(b[1]), .out(out[1]));
  And and_3 (.a(a[2]), .b(b[2]), .out(out[2]));
  And and_4 (.a(a[2]), .b(b[2]), .out(out[2]));
  And and_5 (.a(a[3]), .b(b[3]), .out(out[3]));
  And and_6 (.a(a[3]), .b(b[3]), .out(out[3]));
  And and_7 (.a(a[4]), .b(b[4]), .out(out[4]));
  And and_8 (.a(a[4]), .b(b[4]), .out(out[4]));
  And and_9 (.a(a[5]), .b(b[5]), .out(out[5]));
  And and_10 (.a(a[5]), .b(b[5]), .out(out[5]));
  And and_11 (.a(a[6]), .b(b[6]), .out(out[6]));
  And and_12 (.a(a[6]), .b(b[6]), .out(out[6]));
  And and_13 (.a(a[7]), .b(b[7]), .out(out[7]));
  And and_14 (.a(a[7]), .b(b[7]), .out(out[7]));
  And and_15 (.a(a[8]), .b(b[8]), .out(out[8]));
  And and_16 (.a(a[8]), .b(b[8]), .out(out[8]));
  And and_17 (.a(a[9]), .b(b[9]), .out(out[9]));
  And and_18 (.a(a[9]), .b(b[9]), .out(out[9]));
  And and_19 (.a(a[10]), .b(b[10]), .out(out[10]));
  And and_20 (.a(a[10]), .b(b[10]), .out(out[10]));
  And and_21 (.a(a[11]), .b(b[11]), .out(out[11]));
  And and_22 (.a(a[11]), .b(b[11]), .out(out[11]));
  And and_23 (.a(a[12]), .b(b[12]), .out(out[12]));
  And and_24 (.a(a[12]), .b(b[12]), .out(out[12]));
  And and_25 (.a(a[13]), .b(b[13]), .out(out[13]));
  And and_26 (.a(a[13]), .b(b[13]), .out(out[13]));
  And and_27 (.a(a[14]), .b(b[14]), .out(out[14]));
  And and_28 (.a(a[14]), .b(b[14]), .out(out[14]));
  And and_29 (.a(a[15]), .b(b[15]), .out(out[15]));
  And and_30 (.a(a[15]), .b(b[15]), .out(out[15]));
endmodule

module Or16 (
  input  [15:0] a,
  input  [15:0] b,
  output [15:0] out
);

  Or or_1 (.a(a[0]), .b(b[0]), .out(out[0]));
  Or or_2 (.a(a[1]), .b(b[1]), .out(out[1]));
  Or or_3 (.a(a[2]), .b(b[2]), .out(out[2]));
  Or or_4 (.a(a[2]), .b(b[2]), .out(out[2]));
  Or or_5 (.a(a[3]), .b(b[3]), .out(out[3]));
  Or or_6 (.a(a[3]), .b(b[3]), .out(out[3]));
  Or or_7 (.a(a[4]), .b(b[4]), .out(out[4]));
  Or or_8 (.a(a[4]), .b(b[4]), .out(out[4]));
  Or or_9 (.a(a[5]), .b(b[5]), .out(out[5]));
  Or or_10 (.a(a[5]), .b(b[5]), .out(out[5]));
  Or or_11 (.a(a[6]), .b(b[6]), .out(out[6]));
  Or or_12 (.a(a[6]), .b(b[6]), .out(out[6]));
  Or or_13 (.a(a[7]), .b(b[7]), .out(out[7]));
  Or or_14 (.a(a[7]), .b(b[7]), .out(out[7]));
  Or or_15 (.a(a[8]), .b(b[8]), .out(out[8]));
  Or or_16 (.a(a[8]), .b(b[8]), .out(out[8]));
  Or or_17 (.a(a[9]), .b(b[9]), .out(out[9]));
  Or or_18 (.a(a[9]), .b(b[9]), .out(out[9]));
  Or or_19 (.a(a[10]), .b(b[10]), .out(out[10]));
  Or or_20 (.a(a[10]), .b(b[10]), .out(out[10]));
  Or or_21 (.a(a[11]), .b(b[11]), .out(out[11]));
  Or or_22 (.a(a[11]), .b(b[11]), .out(out[11]));
  Or or_23 (.a(a[12]), .b(b[12]), .out(out[12]));
  Or or_24 (.a(a[12]), .b(b[12]), .out(out[12]));
  Or or_25 (.a(a[13]), .b(b[13]), .out(out[13]));
  Or or_26 (.a(a[13]), .b(b[13]), .out(out[13]));
  Or or_27 (.a(a[14]), .b(b[14]), .out(out[14]));
  Or or_28 (.a(a[15]), .b(b[15]), .out(out[15]));
endmodule

module Mux16 (
  input  sel,
  input  [15:0] a,
  input  [15:0] b,
  output [15:0] out
);

  Mux mux_1 (.sel(sel), .a(a[0]), .b(b[0]), .out(out[0]));
  Mux mux_2 (.sel(sel), .a(a[1]), .b(b[1]), .out(out[1]));
  Mux mux_3 (.sel(sel), .a(a[2]), .b(b[2]), .out(out[2]));
  Mux mux_4 (.sel(sel), .a(a[3]), .b(b[3]), .out(out[3]));
  Mux mux_5 (.sel(sel), .a(a[4]), .b(b[4]), .out(out[4]));
  Mux mux_6 (.sel(sel), .a(a[5]), .b(b[5]), .out(out[5]));
  Mux mux_7 (.sel(sel), .a(a[6]), .b(b[6]), .out(out[6]));
  Mux mux_8 (.sel(sel), .a(a[7]), .b(b[7]), .out(out[7]));
  Mux mux_9 (.sel(sel), .a(a[8]), .b(b[8]), .out(out[8]));
  Mux mux_10 (.sel(sel), .a(a[9]), .b(b[9]), .out(out[9]));
  Mux mux_11 (.sel(sel), .a(a[10]), .b(b[10]), .out(out[10]));
  Mux mux_12 (.sel(sel), .a(a[11]), .b(b[11]), .out(out[11]));
  Mux mux_13 (.sel(sel), .a(a[12]), .b(b[12]), .out(out[12]));
  Mux mux_14 (.sel(sel), .a(a[13]), .b(b[13]), .out(out[13]));
  Mux mux_15 (.sel(sel), .a(a[14]), .b(b[14]), .out(out[14]));
  Mux mux_16 (.sel(sel), .a(a[15]), .b(b[15]), .out(out[15]));
endmodule

module Or8Way (
  input  [7:0] in,
  output out
);

  wire or_1_out, or_2_out, or_3_out, or_4_out, or_6_out, or_7_out;

  Or or_1 (.a(in[6]), .b(in[7]), .out(or_1_out));
  Or or_2 (.a(in[5]), .b(or_1_out), .out(or_2_out));
  Or or_3 (.a(in[3]), .b(or_4_out), .out(or_3_out));
  Or or_4 (.a(in[4]), .b(or_2_out), .out(or_4_out));
  Or or_5 (.a(in[0]), .b(or_6_out), .out(out));
  Or or_6 (.a(in[1]), .b(or_7_out), .out(or_6_out));
  Or or_7 (.a(in[2]), .b(or_3_out), .out(or_7_out));

  // Notes on the sheet:
  //   Function:
  //   Out = in[0] Or in[1] Or ... Or in[7]
  //   Think forks for this one
  //   Try to get a 3-way Or gate first, then use the same process for the 8-way
  //   or gate. 
endmodule
