// Logisim project Computer.circ as structural Verilog: 2 circuits, main circuit Computer
module Computer (
);

  wire and_1_out, and_2_out, Clock, clock_2_out, display, load, or_1_out;
  wire [14:0] Address, demultiplexer_1_out0, demultiplexer_1_out1, demultiplexer_2_out0,
       demultiplexer_2_out1, PC;
  wire [15:0] Input, keyboard_1_p4, memOutput, multiplexer_1_out, multiplexer_3_out, ram_1_dout, rom_1_data,
       screen_1_p1;

  ROM #(.addrWidth(15), .dataWidth(16)) rom_1 (.addr(PC), .data(rom_1_data));
  Clock clock_1 (.out(Clock));
  // CPU cpu_1: pin names not known; wires that end beside it: Clock, rom_1_data, memOutput
  Button button_1 ();  // open: out
  // Probe on Input
  // Probe on Address
  Demultiplexer #(.enable("false"), .width(15)) demultiplexer_1 (
    .out0(demultiplexer_1_out0), .out1(demultiplexer_1_out1), .in(Address), .sel(Address[14]));
  Demultiplexer #(.enable("false"), .width(15)) demultiplexer_2 (
    .out0(demultiplexer_2_out0), .out1(demultiplexer_2_out1), .in(demultiplexer_1_out1), .sel(Address[13]));
  and and_1 (and_1_out, ~Address[14], load);  // AND_Gate
  Clock clock_2 (.out(clock_2_out));
  // Probe on demultiplexer_2_out0[12:0]
  and and_2 (and_2_out, Address[14], ~Address[13], load);  // AND_Gate
  RAM #(.addrWidth(14), .dataWidth(16)) ram_1 (
    .addr(demultiplexer_1_out0[13:0]), .we(and_1_out), .clk(clock_2_out), .din(Input), .dout(ram_1_dout));
  or or_1 (or_1_out, demultiplexer_2_out1[0], demultiplexer_2_out1[1], demultiplexer_2_out1[2], demultiplexer_2_out1[3], demultiplexer_2_out1[4], demultiplexer_2_out1[5], demultiplexer_2_out1[6], demultiplexer_2_out1[7], demultiplexer_2_out1[8], demultiplexer_2_out1[9], demultiplexer_2_out1[10], demultiplexer_2_out1[11], demultiplexer_2_out1[12]);
  // Keyboard keyboard_1: pin names not known; wires that end beside it: demultiplexer_2_out0[12:0], and_2_out, display, keyboard_1_p4
  // Screen screen_1: pin names not known; wires that end beside it: screen_1_p1
  Multiplexer #(.enable("false"), .width(16)) multiplexer_1 (
    .in0(keyboard_1_p4), .in1({16{1'b0}}), .out(multiplexer_1_out), .sel(or_1_out));
  // Probe on ram_1_dout
  Multiplexer #(.enable("false"), .width(16)) multiplexer_2 (
    .in0(ram_1_dout), .in1(multiplexer_3_out), .out(memOutput), .sel(Address[14]));
  // Probe on multiplexer_3_out
  Multiplexer #(.enable("false"), .width(16)) multiplexer_3 (
    .in0(screen_1_p1), .in1(multiplexer_1_out), .out(multiplexer_3_out), .sel(Address[13]));
  // Probe on memOutput

  // Other names for the same wires on the sheet: SMSB = Address[13]; MSB = Address[14]

  // Notes on the sheet:
  //   contents of rom_1 (hex, n*v repeats v):
  //   8015 1080 10c2 1101 38c5 2480 5481 56c1 f000 4004 8015 1080 10c2 1101 1142 38fa 2540 5481 56c1 400f
  //   4000 1184 1143 1b40 6d7d 7e00
  //   First, finish the Memory component.
  //   When that is complete, drag the following components out and wire them together:
  //   - CPU
  //   - ROM (32K)
  //   Then, copy the internals of the Memory component over to this file and wire that up.
  //   The CPU now has a support for a "display" instruction (opcode 1111) which works the following way:
  //   CPU:
  //   	If opcode == 1111, display = 1
  //   	else: display = 0
  //   Screen:
  //   	If display = 1, refresh image from internal memory
  //   	else: do nothing (internal memory will still update if load is 1 though)
  //   For wiring, just connect the display output from the CPU directly to the display input of the Screen
endmodule

module Memory (
  input  [14:0] address,
  input  [15:0] in,
  input  load,
  input  display,
  output [15:0] out
);

  wire and_1_out, and_2_out, clock_1_out, or_1_out;
  wire [14:0] demultiplexer_1_out0, demultiplexer_1_out1, demultiplexer_2_out0, demultiplexer_2_out1;
  wire [15:0] multiplexer_1_out, multiplexer_3_out, ram_1_dout, screen_1_p1;

  Demultiplexer #(.enable("false"), .width(15)) demultiplexer_1 (
    .out0(demultiplexer_1_out0), .out1(demultiplexer_1_out1), .in(address), .sel(address[14]));
  Demultiplexer #(.enable("false"), .width(15)) demultiplexer_2 (
    .out0(demultiplexer_2_out0), .out1(demultiplexer_2_out1), .in(demultiplexer_1_out1), .sel(address[13]));
  and and_1 (and_1_out, ~address[14], load);  // AND_Gate
  Clock clock_1 (.out(clock_1_out));
  // Probe on in
  // Probe on demultiplexer_2_out0[12:0]
  and and_2 (and_2_out, address[14], ~address[13], load);  // AND_Gate
  RAM #(.addrWidth(14), .dataWidth(16)) ram_1 (
    .addr(demultiplexer_1_out0[13:0]), .we(and_1_out), .clk(clock_1_out), .din(in), .dout(ram_1_dout));
  or or_1 (or_1_out, demultiplexer_2_out1[0], demultiplexer_2_out1[1], demultiplexer_2_out1[2], demultiplexer_2_out1[3], demultiplexer_2_out1[4], demultiplexer_2_out1[5], demultiplexer_2_out1[6], demultiplexer_2_out1[7], demultiplexer_2_out1[8], demultiplexer_2_out1[9], demultiplexer_2_out1[10], demultiplexer_2_out1[11], demultiplexer_2_out1[12]);
  // Keyboard keyboard_1: pin names not known
  // Screen screen_1: pin names not known; wires that end beside it: screen_1_p1
  Multiplexer #(.enable("false"), .width(16)) multiplexer_1 (
    .in1({16{1'b0}}), .out(multiplexer_1_out), .sel(or_1_out));  // open: in0
  // Probe on screen_1_p1
  // Probe on multiplexer_1_out
  Multiplexer #(.enable("false"), .width(16)) multiplexer_2 (
    .in0(ram_1_dout), .in1(multiplexer_3_out), .out(out), .sel(address[14]));
  Multiplexer #(.enable("false"), .width(16)) multiplexer_3 (
    .in0(screen_1_p1), .in1(multiplexer_1_out), .out(multiplexer_3_out), .sel(address[13]));

  // Other names for the same wires on the sheet: SMSB = address[13]; MSB = address[14]; Input[15:0] = in

  // Notes on the sheet:
  //   Memory
  //   Use a 16K RAM and built in Keyboard/Screen
endmodule
