// Logisim project Assignment3.circ as structural Verilog: 3 circuits, main circuit ALU
module ALU (
  input  [2:0] op,
  input  [15:0] a,
  input  [15:0] b,
  output zero,
  output [15:0] out
);

  wire or_1_out, or_2_out, or_3_out, or_4_out, or_5_out, or_7_out, or_8_out, or_9_out, or_10_out, or_11_out,
       or_12_out, or_13_out, or_14_out, or_15_out, or_16_out;
  wire [14:0] adder_1_out;
  wire [15:0] and_1_out, multiplexer_1_out, multiplexer_3_out, not_1_out, or_6_out;
  wire [15:15] adder_1_out_2;

  Multiplexer #(.enable("false"), .width(16)) multiplexer_1 (
    .in0(b), .in1(not_1_out), .out(multiplexer_1_out), .sel(op[2]));
  assign not_1_out = ~b;  // NOT_Gate not_1, 16 bits wide
  or or_1 (or_1_out, out[13], out[12]);
  or or_2 (or_2_out, out[15], out[14]);
  or or_3 (or_3_out, or_2_out, or_1_out);
  or or_4 (or_4_out, out[11], out[10]);
  or or_5 (or_5_out, or_4_out, or_7_out);
  assign and_1_out = a & multiplexer_1_out;  // AND_Gate and_1, 16 bits wide
  assign or_6_out = a | multiplexer_1_out;  // OR_Gate or_6, 16 bits wide
  Adder #(.width(16)) adder_1 (
    .a(a), .b(multiplexer_1_out), .out({adder_1_out_2[15], adder_1_out}), .cin(op[2]));  // open: cout
  or or_7 (or_7_out, out[9], out[8]);
  or or_8 (or_8_out, out[7], out[6]);
  or or_9 (or_9_out, or_8_out, or_11_out);
  or or_10 (or_10_out, or_3_out, or_5_out);
  or or_11 (or_11_out, out[5], out[4]);
  or or_12 (or_12_out, out[3], out[2]);
  or or_13 (or_13_out, or_15_out, or_9_out);
  Multiplexer #(.enable("false"), .select(2), .width(16)) multiplexer_2 (
    .in0(and_1_out), .in1(or_6_out), .in2({adder_1_out_2[15], adder_1_out}), .in3(multiplexer_3_out),
    .out(out), .sel(op[1:0]));
  Multiplexer #(.enable("false"), .width(16)) multiplexer_3 (
    .in0({16{1'b0}}), .in1(16'h1), .out(multiplexer_3_out), .sel(adder_1_out_2[15]));
  or or_14 (or_14_out, out[1], out[0]);
  or or_15 (or_15_out, or_12_out, or_14_out);
  or or_16 (or_16_out, or_10_out, or_13_out);
  not not_2 (zero, or_16_out);

  // Notes on the sheet:
  //   This is just a 16 bit or gate that returns 1 if any inputs are 1
  //   This is the brawn of the computer.
  //   The ALU is responsible for performing almost every arithmetic or logical operation
  //   in a modern computer. A premade ALU is provided in the AL
  //   Function:
  //   - If (op == 000), set out = a & b (bitwise AND)
  //   - If (op == 001), set out = a || b (bitwise OR)
  //   - If (op == 010), set out = a + b (addition)
  //   - If (op == 100), set out = a & !b (a and not b)
  //   - If (op == 101), set out = a || !b (a or not b)
  //   - If (op == 110), set out = a - b (subtraction)
  //   - If (op == 111), set out = 0000000000000001 if a < b 
  //   										else 0000000000000000 (set-on-less-than)
  //   - Zero = 1 if (out == 0) else Zero = 0
  //   Hints:
  //   - Tackle the opcodes in the groups described above (first three, next two, and so on)
  //   - For the first three, ignore the MSB of the opcode.
  //   - For the next two, use the MSB to control between negating or not negating B
  //   - At this point, subtraction should be almost implemented.
  //   - Think about two's complement. You have half of two's complement implemented currently.
  //   - You just need to make one connection to fully implement two's complement subtraction
  //   - To determine if A < B, you can use subtraction. 
  //   - If A < B, then A - B should be negative.
  //   - Think about how to determine if a number is negative
  //   - Use that to select between the output for SLT (set on less than)
  //   - Finally, determine how to set the Zero output. You might need to use a splitter for this
endmodule

module Bit (
  input  load,
  input  in,
  output out
);

  wire and_1_out, clock_1_out;

  Clock clock_1 (.out(clock_1_out));
  and and_1 (and_1_out, clock_1_out, load);
  D_Flip_Flop d_ff_1 (.D(in), .clk(and_1_out), .Q(out));  // open: Qn, preset, reset

  // Notes on the sheet:
  //   Function:
  //   if load(t-1) then out(t) = in(t-1)
  //   else out(t) = out(t-1)
  //   More simply, when load = 1, 'out' will store the value of 'in' every rising clock edge. When load = 0, 
  //   'out' will not change, even when 'in' changes.
  //   You do not need to use the S, R, or Q-complement ports of the D-FlipFlop
  //   The implementation of this can be found in the lecture slides. 
  //   Take some time to play around with this component (especially the clock) and see how it works.
  //   If you want the clock to automatically tick, go to Simulate>Auto Tick Enabled. You can change
  //   the speed of the clock with Simulate>Auto Tick Frequency
  //   To test this, I recommend turning the Clock to Auto-Tick and verifying that when load is 1, you can
  //   load a value into the flip flop, and when load is 0, the flip flop doesn't change it's value
endmodule

module Register (
  input  load,
  input  [15:0] in,
  output [15:0] out
);

  Bit bit_1 (.load(load), .in(in[0]), .out(out[0]));
  Bit bit_2 (.load(load), .in(in[1]), .out(out[1]));
  Bit bit_3 (.load(load), .in(in[2]), .out(out[2]));
  Bit bit_4 (.load(load), .in(in[3]), .out(out[3]));
  Bit bit_5 (.load(load), .in(in[4]), .out(out[4]));
  Bit bit_6 (.load(load), .in(in[5]), .out(out[5]));
  Bit bit_7 (.load(load), .in(in[6]), .out(out[6]));
  Bit bit_8 (.load(load), .in(in[7]), .out(out[7]));
  Bit bit_9 (.load(load), .in(in[8]), .out(out[8]));
  Bit bit_10 (.load(load), .in(in[9]), .out(out[9]));
  Bit bit_11 (.load(load), .in(in[10]), .out(out[10]));
  Bit bit_12 (.load(load), .in(in[11]), .out(out[11]));
  Bit bit_13 (.load(load), .in(in[12]), .out(out[12]));
  Bit bit_14 (.load(load), .in(in[13]), .out(out[13]));
  Bit bit_15 (.load(load), .in(in[14]), .out(out[14]));
  Bit bit_16 (.load(load), .in(in[15]), .out(out[15]));

  // Notes on the sheet:
  //   Function:
  //   if load(t-1) then out(t) = in(t-1)
  //   else out(t) = out(t-1)
  //   More simply, when load = 1, 'out' will store the value of 'in' every rising clock edge. When load = 0, 
  //   'out' will not change, even when 'in' changes.
  //   The construction of a w-bit Register chip from 1-bit registers is straightforward. All you have
  //   to do is construct an array of w Bit gates and feed the register's load input to every one of them.
  //   To test this, I recommend turning the Clock to Auto-Tick. When load is 1, you should be able to load a 
  //   16-bit value into the register, when you turn load off, that value should remain in place.
endmodule
