// Logisim project Assignment8.circ as structural Verilog: 1 circuit, main circuit Control
module Control (
  input  [3:0] Opcode,
  input  [2:0] Funct,
  output MemtoReg,
  output Branch,
  output MemWrite,
  output RegWrite,
  output ALUSrc,
  output RegDst,
  output [2:0] ALUOp
);

  Multiplexer #(.enable("false"), .select(3), .width(3)) multiplexer_1 (
    .in0(Funct), .in1(3'b010), .in2(3'b010), .in3(3'b110), .in5(3'b010), .out(ALUOp), .sel(Opcode[2:0]));  // open: in4, in6, in7
  and and_1 (MemtoReg, ~Opcode[2], ~Opcode[1], Opcode[0]);  // AND_Gate
  and and_2 (Branch, Opcode[1], Opcode[0]);
  and and_3 (MemWrite, Opcode[1], ~Opcode[0]);  // AND_Gate
  not not_1 (RegWrite, Opcode[1]);
  xor xor_1 (ALUSrc, Opcode[0], Opcode[1]);
  and and_4 (RegDst, ~Opcode[0], ~Opcode[1], ~Opcode[2], ~Opcode[3]);  // AND_Gate
endmodule
