// Logisim project CPU.circ as structural Verilog: 1 circuit, main circuit main
module main (
  input  in_1
);

  wire alu_1_p7, ALUSrc, and_1_out, BEQ, BNE, Clock, inc16_2_p3, J, JAL, JR, MemtoReg, MemWrite,
       multiplexer_8_out, not_1_out, or_1_out, or_2_out, RegDest, RegWrite;
  wire [2:0] ALUOp, multiplexer_1_out;
  wire [13:0] alu_1_p5;
  wire [15:0] adder_1_out, alu_1_p2, alu_1_p6, bit_extender_1_out, IMM, inc16_1_p1, inc16_1_p2, inc16_2_p2,
       Memory_dout, multiplexer_2_out, multiplexer_4_out, multiplexer_6_out, multiplexer_7_out,
       multiplexer_9_out, rom_1_data, undriven;
  wire [15:14] alu_1_p5_2;

  // Inc16 inc16_1: pin names not known; wires that end beside it: inc16_1_p1, inc16_1_p2
  ROM #(.addrWidth(16), .dataWidth(16)) rom_1 (.addr(inc16_1_p1), .data(rom_1_data));
  Register #(.width(16)) register_1 (.D(multiplexer_7_out), .en(1'b1), .Q(inc16_1_p1), .clk(Clock), .clr(in_1));
  Clock clock_1 (.out(Clock));
  assign bit_extender_1_out = {{4{1'b0}}, rom_1_data[11:0]};  // Bit_Extender bit_extender_1
  // Inc16 inc16_2: pin names not known; wires that end beside it: inc16_1_p1, inc16_2_p2, inc16_2_p3
  // Probe on bit_extender_1_out
  // Probe on rom_1_data[15:12]
  // Probe on rom_1_data
  // Control control_1: pin names not known; wires that end beside it: rom_1_data[15:12], rom_1_data[2:0], BNE, BEQ, J, JAL
  // Probe on rom_1_data[11:9]
  // Probe on rom_1_data[8:6]
  Multiplexer #(.enable("false"), .width(3)) multiplexer_1 (
    .in0(rom_1_data[8:6]), .in1(rom_1_data[5:3]), .out(multiplexer_1_out), .sel(RegDest));
  // Probe on rom_1_data[5:3]
  Multiplexer #(.enable("false"), .width(16)) multiplexer_2 (
    .in0(multiplexer_9_out), .in1(inc16_2_p2), .out(multiplexer_2_out), .sel(JAL));
  // Probe on rom_1_data[5:0]
  // RegisterFile registerfile_1: pin names not known; wires that end beside it: JR, MemtoReg, MemWrite, RegWrite, ALUSrc, RegDest, ALUOp, rom_1_data[11:9], rom_1_data[8:6], multiplexer_2_out, Clock, RegWrite
  Multiplexer #(.enable("false"), .width(3)) multiplexer_3 (
    .in0(multiplexer_1_out), .in1(3'b111), .sel(JAL));  // open: out
  assign IMM = {{10{rom_1_data[5]}}, rom_1_data[5:0]};  // Bit_Extender bit_extender_2
  Multiplexer #(.enable("false"), .width(16)) multiplexer_4 (
    .in0(inc16_1_p2), .in1(adder_1_out), .out(multiplexer_4_out), .sel(and_1_out));
  Adder #(.width(16)) adder_1 (.a(inc16_1_p2), .b(IMM), .out(adder_1_out));  // open: cin, cout
  and and_1 (and_1_out, or_1_out, multiplexer_8_out);
  or or_1 (or_1_out, BNE, BEQ);
  // Probe on alu_1_p2
  // ALU alu_1: pin names not known; wires that end beside it: in_1, alu_1_p2, alu_1_p2, ALUOp, {alu_1_p5_2, alu_1_p5}, alu_1_p6, alu_1_p7
  // Probe on alu_1_p6
  Multiplexer #(.enable("false"), .width(16)) multiplexer_5 (.in0(undriven), .in1(IMM), .out(alu_1_p6), .sel(ALUSrc));
  Multiplexer #(.enable("false"), .width(16)) multiplexer_6 (
    .in0(multiplexer_4_out), .in1(bit_extender_1_out), .out(multiplexer_6_out), .sel(or_2_out));
  or or_2 (or_2_out, J, JAL);
  Multiplexer #(.enable("false"), .width(16)) multiplexer_7 (
    .in0(multiplexer_6_out), .in1(alu_1_p2), .out(multiplexer_7_out), .sel(JR));
  not not_1 (not_1_out, alu_1_p7);
  Multiplexer #(.enable("false")) multiplexer_8 (.in0(not_1_out), .in1(alu_1_p7), .out(multiplexer_8_out), .sel(BEQ));
  RAM #(.addrWidth(14), .dataWidth(16)) Memory (
    .addr(alu_1_p5), .we(MemWrite), .clk(Clock), .din(undriven), .dout(Memory_dout));
  Multiplexer #(.enable("false"), .width(16)) multiplexer_9 (
    .in0({alu_1_p5_2, alu_1_p5}), .in1(Memory_dout), .out(multiplexer_9_out), .sel(MemtoReg));

  // Notes on the sheet:
  //   contents of rom_1 (hex, n*v repeats v):
  //   5040 5081 5100 2041 1140 3b06 2881 5580 452 c0a 5901 3039
endmodule
